// Logisim project circuito.circ as structural Verilog: 10 circuits, main circuit main
module main (
  input  in_1
);

  wire aa, ab, ac, ad, ae, af, ag, and_2_out, ba, bb, bc, bd, be, bf, bg, ca, cb, cc, cd, ce, cf, cg,
       clock_1_out, comparator_1_lt, da, db, dc, dd, de, df, dg, ea, eb, ec, ed, ee, ef, eg, fa, fb, fc, fd,
       fe, ff, fg, ga, gb, gc, gd, ge, gf, gg, ha, hb, hc, hd, he, hf, hg, j_k_ff_1_q, j_k_ff_1_qn, ja, jb,
       jc, jd, je, jf, jg, ka, kb, kc, kd, ke, kf, kg, la, lb, lc, ld, le, lf, lg, maquina_estados_1_z,
       not_1_out, not_2_out, not_3_out, or_1_out, reloj, S_V_1_S, S_V_2_S, salida_suma;
  wire [1:0] bit_extender_1_out;
  wire [3:0] contador_par_1_salida_par, estado_maquina, fase, view_number_1_centenas, view_number_1_decenas,
       view_number_1_unidades, view_number_2_centenas, view_number_2_decenas, view_number_2_unidades,
       view_number_3_centenas, view_number_3_decenas, view_number_3_unidades, view_number_4_unidades,
       view_number_5_unidades;
  wire [7:0] bit_extender_2_out, bit_extender_3_out, S_V_1, S_V_2, suma;

  _7_Segment_Display u_7_segment_display_1 (.g(S_V_1_S));  // open: f, a, b, e, d, c, dp
  _7_Segment_Display u_7_segment_display_2 (.g(salida_suma));  // open: f, a, b, e, d, c, dp
  Clock clock_1 (.out(clock_1_out));
  and and_1 (reloj, clock_1_out, comparator_1_lt);
  _7_Segment_Display u_7_segment_display_3 (.g(ag), .f(af), .a(aa), .b(ab), .e(ae), .d(ad), .c(ac));  // open: dp
  _7_Segment_Display u_7_segment_display_4 (.g(gg), .f(gf), .a(ga), .b(gb), .e(ge), .d(gd), .c(gc));  // open: dp
  Comparator #(.width(4)) comparator_1 (.a(fase), .b(4'b0011), .lt(comparator_1_lt));  // open: gt, eq
  not not_1 (not_1_out, reloj);
  _7_Segment_Display u_7_segment_display_5 (.g(bg), .f(bf), .a(ba), .b(bb), .e(be), .d(bd), .c(bc));  // open: dp
  _7_Segment_Display u_7_segment_display_6 (.g(hg), .f(hf), .a(ha), .b(hb), .e(he), .d(hd), .c(hc));  // open: dp
  _7_Segment_Display u_7_segment_display_7 (.g(cg), .f(cf), .a(ca), .b(cb), .e(ce), .d(cd), .c(cc));  // open: dp
  _7_Segment_Display u_7_segment_display_8 (.g(jg), .f(jf), .a(ja), .b(jb), .e(je), .d(jd), .c(jc));  // open: dp
  contador_par contador_par_1 (.reset(or_1_out), .clock(not_1_out), .salida_par(contador_par_1_salida_par));
  sumador8 sumador8_1 (.A(S_V_1), .B(S_V_2), .out_5(suma));  // open: Cin, out_4
  not not_2 (not_2_out, reloj);
  and and_2 (and_2_out, ~reloj, j_k_ff_1_q);  // AND_Gate
  _7_Segment_Display u_7_segment_display_9 (.g(S_V_2_S));  // open: f, a, b, e, d, c, dp
  or or_1 (or_1_out, in_1, and_2_out);
  _7_Segment_Display u_7_segment_display_10 (.g(dg), .f(df), .a(da), .b(db), .e(de), .d(dd), .c(dc));  // open: dp
  _7_Segment_Display u_7_segment_display_11 (.g(eg), .f(ef), .a(ea), .b(eb), .e(ee), .d(ed), .c(ec));  // open: dp
  _7_Segment_Display u_7_segment_display_12 (.g(kg), .f(kf), .a(ka), .b(kb), .e(ke), .d(kd), .c(kc));  // open: dp
  vector vector_1 (
    .reloj(reloj), .reset(in_1), .posicion_salida(contador_par_1_salida_par), .numero_entrada(suma),
    .posicion_entrada(estado_maquina), .salida_posicion_1(S_V_1), .salida_posicion_2(S_V_2));
  contador_unidad contador_unidad_1 (
    .entrada_contador(1'b1), .clock(not_2_out), .reset(or_1_out), .out_4(estado_maquina));
  _7_Segment_Display u_7_segment_display_13 (.g(fg), .f(ff), .a(fa), .b(fb), .e(fe), .d(fd), .c(fc));  // open: dp
  J_K_Flip_Flop j_k_ff_1 (
    .J(maquina_estados_1_z), .K(j_k_ff_1_qn), .clk(reloj), .Q(j_k_ff_1_q), .Qn(j_k_ff_1_qn), .reset(or_1_out));  // open: preset
  not not_3 (not_3_out, reloj);
  _7_Segment_Display u_7_segment_display_14 (.g(lg), .f(lf), .a(la), .b(lb), .e(le), .d(ld), .c(lc));  // open: dp
  contador_unidad contador_unidad_2 (
    .entrada_contador(maquina_estados_1_z), .clock(not_3_out), .reset(in_1), .out_4(fase));
  maquina_estados maquina_estados_1 (.Reset(in_1), .Clock(reloj), .Fase(bit_extender_1_out), .Z(maquina_estados_1_z));
  Bit_Extender #(.in_width(4), .out_width(2)) bit_extender_1 (.in(fase), .out(bit_extender_1_out));
  assign bit_extender_2_out = {{4{fase[3]}}, fase};  // Bit_Extender bit_extender_2
  view_number view_number_1 (
    .in_1(S_V_1), .Signo(S_V_1_S), .centenas(view_number_1_centenas), .Decenas(view_number_1_decenas),
    .Unidades(view_number_1_unidades));
  view_number view_number_2 (
    .in_1(S_V_2), .Signo(S_V_2_S), .centenas(view_number_2_centenas), .Decenas(view_number_2_decenas),
    .Unidades(view_number_2_unidades));
  view_number view_number_3 (
    .in_1(suma), .Signo(salida_suma), .centenas(view_number_3_centenas), .Decenas(view_number_3_decenas),
    .Unidades(view_number_3_unidades));
  assign bit_extender_3_out = {{4{estado_maquina[3]}}, estado_maquina};  // Bit_Extender bit_extender_3
  view_number view_number_4 (
    .in_1(bit_extender_2_out), .Unidades(view_number_4_unidades));  // open: Signo, centenas, Decenas
  deco_segmento deco_segmento_1 (
    .numero(view_number_1_centenas), .a(aa), .b(ab), .c(ac), .d(ad), .e(ae), .f(af), .g(ag));
  deco_segmento deco_segmento_2 (
    .numero(view_number_1_unidades), .a(ca), .b(cb), .c(cc), .d(cd), .e(ce), .f(cf), .g(cg));
  deco_segmento deco_segmento_3 (
    .numero(view_number_2_centenas), .a(da), .b(db), .c(dc), .d(dd), .e(de), .f(df), .g(dg));
  deco_segmento deco_segmento_4 (
    .numero(view_number_2_unidades), .a(fa), .b(fb), .c(fc), .d(fd), .e(fe), .f(ff), .g(fg));
  deco_segmento deco_segmento_5 (
    .numero(view_number_3_centenas), .a(ga), .b(gb), .c(gc), .d(gd), .e(ge), .f(gf), .g(gg));
  deco_segmento deco_segmento_6 (
    .numero(view_number_3_unidades), .a(ja), .b(jb), .c(jc), .d(jd), .e(je), .f(jf), .g(jg));
  deco_segmento deco_segmento_7 (
    .numero(view_number_4_unidades), .a(ka), .b(kb), .c(kc), .d(kd), .e(ke), .f(kf), .g(kg));
  view_number view_number_5 (
    .in_1(bit_extender_3_out), .Unidades(view_number_5_unidades));  // open: Signo, centenas, Decenas
  deco_segmento deco_segmento_8 (
    .numero(view_number_1_decenas), .a(ba), .b(bb), .c(bc), .d(bd), .e(be), .f(bf), .g(bg));
  deco_segmento deco_segmento_9 (
    .numero(view_number_2_decenas), .a(ea), .b(eb), .c(ec), .d(ed), .e(ee), .f(ef), .g(eg));
  deco_segmento deco_segmento_10 (
    .numero(view_number_3_decenas), .a(ha), .b(hb), .c(hc), .d(hd), .e(he), .f(hf), .g(hg));
  deco_segmento deco_segmento_11 (
    .numero(view_number_5_unidades), .a(la), .b(lb), .c(lc), .d(ld), .e(le), .f(lf), .g(lg));

  // Other names for the same wires on the sheet: reset = in_1

  // Notes on the sheet:
  //   Numero (n) del vector
  //   Suma de los numeros (n) y (n+1)
  //   Numero (n+1) del vector
  //   Fase del algoritmo
  //   Posicion entrada
  //   Estado actual de la maquina
  //   Visualizadores del arreglo, salidas n y n+1
  //   visualizador de la suma
  //   Fase del algoritmo
  //   Estado maquina
endmodule

module arreglo_8bits (
  input  reset,
  input  reloj,
  input  [7:0] numero_entrada,
  input  [7:0] valor,
  output [7:0] numero_salida
);

  wire and_1_out, and_2_out, and_11_out, and_12_out, and_13_out, and_14_out, and_15_out, and_16_out, B0, B1,
       B2, B3, B4, B5, B6, B7, j_k_ff_1_qn, j_k_ff_2_qn, j_k_ff_3_qn, j_k_ff_4_qn, j_k_ff_5_qn, j_k_ff_6_qn,
       j_k_ff_7_qn, j_k_ff_8_qn;

  J_K_Flip_Flop j_k_ff_1 (
    .J(numero_entrada[7]), .K(and_1_out), .clk(reloj), .Q(numero_salida[7]), .Qn(j_k_ff_1_qn), .preset(B7),
    .reset(reset));
  and and_1 (and_1_out, ~j_k_ff_1_qn, ~numero_entrada[7], numero_salida[7]);  // AND_Gate
  J_K_Flip_Flop j_k_ff_2 (
    .J(numero_entrada[6]), .K(and_2_out), .clk(reloj), .Q(numero_salida[6]), .Qn(j_k_ff_2_qn), .preset(B6),
    .reset(reset));
  and and_2 (and_2_out, ~j_k_ff_2_qn, ~numero_entrada[6], numero_salida[6]);  // AND_Gate
  J_K_Flip_Flop j_k_ff_3 (
    .J(numero_entrada[5]), .K(and_11_out), .clk(reloj), .Q(numero_salida[5]), .Qn(j_k_ff_3_qn), .preset(B5),
    .reset(reset));
  and and_3 (B0, reset, valor[0]);
  and and_4 (B1, reset, valor[1]);
  and and_5 (B2, reset, valor[2]);
  and and_6 (B3, reset, valor[3]);
  and and_7 (B4, reset, valor[4]);
  and and_8 (B5, reset, valor[5]);
  and and_9 (B6, reset, valor[6]);
  and and_10 (B7, reset, valor[7]);
  J_K_Flip_Flop j_k_ff_4 (
    .J(numero_entrada[4]), .K(and_12_out), .clk(reloj), .Q(numero_salida[4]), .Qn(j_k_ff_4_qn), .preset(B4),
    .reset(reset));
  and and_11 (and_11_out, ~j_k_ff_3_qn, ~numero_entrada[5], numero_salida[5]);  // AND_Gate
  and and_12 (and_12_out, ~j_k_ff_4_qn, ~numero_entrada[4], numero_salida[4]);  // AND_Gate
  J_K_Flip_Flop j_k_ff_5 (
    .J(numero_entrada[3]), .K(and_13_out), .clk(reloj), .Q(numero_salida[3]), .Qn(j_k_ff_5_qn), .preset(B3),
    .reset(reset));
  and and_13 (and_13_out, ~j_k_ff_5_qn, ~numero_entrada[3], numero_salida[3]);  // AND_Gate
  J_K_Flip_Flop j_k_ff_6 (
    .J(numero_entrada[2]), .K(and_14_out), .clk(reloj), .Q(numero_salida[2]), .Qn(j_k_ff_6_qn), .preset(B2),
    .reset(reset));
  and and_14 (and_14_out, ~j_k_ff_6_qn, ~numero_entrada[2], numero_salida[2]);  // AND_Gate
  J_K_Flip_Flop j_k_ff_7 (
    .J(numero_entrada[1]), .K(and_15_out), .clk(reloj), .Q(numero_salida[1]), .Qn(j_k_ff_7_qn), .preset(B1),
    .reset(reset));
  and and_15 (and_15_out, ~j_k_ff_7_qn, ~numero_entrada[1], numero_salida[1]);  // AND_Gate
  J_K_Flip_Flop j_k_ff_8 (
    .J(numero_entrada[0]), .K(and_16_out), .clk(reloj), .Q(numero_salida[0]), .Qn(j_k_ff_8_qn), .preset(B0),
    .reset(reset));
  and and_16 (and_16_out, ~j_k_ff_8_qn, ~numero_entrada[0], numero_salida[0]);  // AND_Gate

  // Other names for the same wires on the sheet: A0 = numero_entrada[0]; A1 = numero_entrada[1];
  //   A2 = numero_entrada[2]; A3 = numero_entrada[3]; A4 = numero_entrada[4]; A5 = numero_entrada[5];
  //   A6 = numero_entrada[6]; A7 = numero_entrada[7]; S0 = numero_salida[0]; S1 = numero_salida[1];
  //   S2 = numero_salida[2]; S3 = numero_salida[3]; S4 = numero_salida[4]; S5 = numero_salida[5];
  //   S6 = numero_salida[6]; S7 = numero_salida[7]
endmodule

module vector (
  input  reloj,
  input  reset,
  input  [3:0] posicion_salida,
  input  [7:0] numero_entrada,
  input  [3:0] posicion_entrada,
  output [7:0] salida_posicion_1,
  output [7:0] salida_posicion_2
);

  wire comparator_1_eq, comparator_2_eq, comparator_3_eq, comparator_4_eq, comparator_5_eq, comparator_6_eq,
       comparator_7_eq, comparator_8_eq, comparator_9_eq, comparator_10_eq, comparator_11_eq,
       comparator_12_eq, comparator_13_eq, comparator_14_eq, comparator_15_eq, comparator_16_eq, r0, r1, r2,
       r3, r4, r5, r6, r7, r8, r9, r10, r11, r12, r13, r14, r15;
  wire [3:0] bit_extender_3_out;
  wire [7:0] A0, A1, A2, A3, A4, A5, A6, A7, A8, A9, A10, A11, A12, A13, A14, A15, bit_extender_1_out,
       bit_extender_2_out, S0, S1, S2, S3, S4, S5, S6, S7, S8, S9, S10, S11, S12, S13, S14, S15,
       sumador8_1_out_5;

  Comparator #(.width(4)) comparator_1 (.a(4'b0000), .b(posicion_entrada), .eq(comparator_1_eq));  // open: gt, lt
  Comparator #(.width(4)) comparator_2 (.a(4'b0001), .b(posicion_entrada), .eq(comparator_2_eq));  // open: gt, lt
  Comparator #(.width(4)) comparator_3 (.a(4'b0010), .b(posicion_entrada), .eq(comparator_3_eq));  // open: gt, lt
  Comparator #(.width(4)) comparator_4 (.a(4'b0011), .b(posicion_entrada), .eq(comparator_4_eq));  // open: gt, lt
  Comparator #(.width(4)) comparator_5 (.a(4'b0100), .b(posicion_entrada), .eq(comparator_5_eq));  // open: gt, lt
  Comparator #(.width(4)) comparator_6 (.a(4'b0101), .b(posicion_entrada), .eq(comparator_6_eq));  // open: gt, lt
  Comparator #(.width(4)) comparator_7 (.a(4'b0110), .b(posicion_entrada), .eq(comparator_7_eq));  // open: gt, lt
  Comparator #(.width(4)) comparator_8 (.a(4'b0111), .b(posicion_entrada), .eq(comparator_8_eq));  // open: gt, lt
  Demultiplexer #(.select(4), .width(8)) demultiplexer_1 (
    .out0(A0), .out1(A1), .out2(A2), .out3(A3), .out4(A4), .out5(A5), .out6(A6), .out7(A7), .out8(A8),
    .out9(A9), .out10(A10), .out11(A11), .out12(A12), .out13(A13), .out14(A14), .out15(A15),
    .in(numero_entrada), .sel(posicion_entrada));
  and and_1 (r0, comparator_1_eq, reloj);
  and and_2 (r1, comparator_2_eq, reloj);
  and and_3 (r2, comparator_3_eq, reloj);
  and and_4 (r3, comparator_4_eq, reloj);
  and and_5 (r4, comparator_5_eq, reloj);
  and and_6 (r5, comparator_6_eq, reloj);
  and and_7 (r6, comparator_7_eq, reloj);
  and and_8 (r7, comparator_8_eq, reloj);
  Comparator #(.width(4)) comparator_9 (.a(4'b1000), .b(posicion_entrada), .eq(comparator_9_eq));  // open: gt, lt
  Comparator #(.width(4)) comparator_10 (.a(4'b1001), .b(posicion_entrada), .eq(comparator_10_eq));  // open: gt, lt
  Comparator #(.width(4)) comparator_11 (.a(4'b1010), .b(posicion_entrada), .eq(comparator_11_eq));  // open: gt, lt
  Comparator #(.width(4)) comparator_12 (.a(4'b1011), .b(posicion_entrada), .eq(comparator_12_eq));  // open: gt, lt
  Comparator #(.width(4)) comparator_13 (.a(4'b1100), .b(posicion_entrada), .eq(comparator_13_eq));  // open: gt, lt
  Comparator #(.width(4)) comparator_14 (.a(4'b1101), .b(posicion_entrada), .eq(comparator_14_eq));  // open: gt, lt
  Comparator #(.width(4)) comparator_15 (.a(4'b1110), .b(posicion_entrada), .eq(comparator_15_eq));  // open: gt, lt
  Comparator #(.width(4)) comparator_16 (.a(4'b1111), .b(posicion_entrada), .eq(comparator_16_eq));  // open: gt, lt
  and and_9 (r8, comparator_9_eq, reloj);
  and and_10 (r9, comparator_10_eq, reloj);
  and and_11 (r10, comparator_11_eq, reloj);
  and and_12 (r11, comparator_12_eq, reloj);
  and and_13 (r12, comparator_13_eq, reloj);
  and and_14 (r13, comparator_14_eq, reloj);
  and and_15 (r14, comparator_15_eq, reloj);
  and and_16 (r15, comparator_16_eq, reloj);
  arreglo_8bits position_0 (.reset(reset), .reloj(r0), .numero_entrada(A0), .valor({8{1'b0}}), .numero_salida(S0));
  arreglo_8bits position_1 (.reset(reset), .reloj(r1), .numero_entrada(A1), .valor(8'h1), .numero_salida(S1));
  arreglo_8bits position_2 (.reset(reset), .reloj(r2), .numero_entrada(A2), .valor(8'hfe), .numero_salida(S2));
  arreglo_8bits position_3 (.reset(reset), .reloj(r3), .numero_entrada(A3), .valor(8'h3), .numero_salida(S3));
  arreglo_8bits position_4 (.reset(reset), .reloj(r4), .numero_entrada(A4), .valor(8'h4), .numero_salida(S4));
  arreglo_8bits position_5 (.reset(reset), .reloj(r5), .numero_entrada(A5), .valor(8'hfb), .numero_salida(S5));
  arreglo_8bits position_6 (.reset(reset), .reloj(r6), .numero_entrada(A6), .valor(8'h6), .numero_salida(S6));
  arreglo_8bits position_7 (.reset(reset), .reloj(r7), .numero_entrada(A7), .valor(8'h7), .numero_salida(S7));
  arreglo_8bits position_8 (.reset(reset), .reloj(r8), .numero_entrada(A8), .valor(8'h8), .numero_salida(S8));
  arreglo_8bits position_9 (.reset(reset), .reloj(r9), .numero_entrada(A9), .valor(8'h9), .numero_salida(S9));
  arreglo_8bits position_10 (.reset(reset), .reloj(r10), .numero_entrada(A10), .valor(8'ha), .numero_salida(S10));
  arreglo_8bits position_11 (.reset(reset), .reloj(r11), .numero_entrada(A11), .valor(8'hb), .numero_salida(S11));
  arreglo_8bits position_12 (.reset(reset), .reloj(r12), .numero_entrada(A12), .valor(8'hc), .numero_salida(S12));
  arreglo_8bits position_13 (.reset(reset), .reloj(r13), .numero_entrada(A13), .valor(8'hd), .numero_salida(S13));
  arreglo_8bits position_14 (.reset(reset), .reloj(r14), .numero_entrada(A14), .valor(8'he), .numero_salida(S14));
  arreglo_8bits position_15 (.reset(reset), .reloj(r15), .numero_entrada(A15), .valor(8'hf), .numero_salida(S15));
  assign bit_extender_1_out = {{4{posicion_salida[3]}}, posicion_salida};  // Bit_Extender bit_extender_1
  assign bit_extender_2_out = {{4{1'b0}}, 4'b0001};  // Bit_Extender bit_extender_2
  Multiplexer #(.select(4), .width(8)) multiplexer_1 (
    .in0(S0), .in1(S1), .in2(S2), .in3(S3), .in4(S4), .in5(S5), .in6(S6), .in7(S7), .in8(S8), .in9(S9),
    .in10(S10), .in11(S11), .in12(S12), .in13(S13), .in14(S14), .in15(S15), .out(salida_posicion_1),
    .sel(posicion_salida));
  Multiplexer #(.select(4), .width(8)) multiplexer_2 (
    .in0(S0), .in1(S1), .in2(S2), .in3(S3), .in4(S4), .in5(S5), .in6(S6), .in7(S7), .in8(S8), .in9(S9),
    .in10(S10), .in11(S11), .in12(S12), .in13(S13), .in14(S14), .in15(S15), .out(salida_posicion_2),
    .sel(bit_extender_3_out));
  sumador8 sumador8_1 (
    .A(bit_extender_1_out), .B(bit_extender_2_out), .Cin(1'b0), .out_5(sumador8_1_out_5));  // open: out_4
  Bit_Extender #(.out_width(4)) bit_extender_3 (.in(sumador8_1_out_5), .out(bit_extender_3_out));

  // Other names for the same wires on the sheet: p_in[3:0] = posicion_entrada
endmodule

module deco_segmento (
  input  [3:0] numero,
  output a,
  output b,
  output c,
  output d,
  output e,
  output f,
  output g
);

  wire and_1_out, and_2_out, and_3_out, and_4_out, and_5_out, and_6_out, and_7_out, and_8_out, and_9_out,
       and_10_out, and_11_out, and_12_out, and_13_out, and_14_out, and_15_out, and_16_out, not_1_out,
       not_2_out, not_3_out;

  not not_1 (not_1_out, numero[2]);
  not not_2 (not_2_out, numero[1]);
  not not_3 (not_3_out, numero[0]);
  and and_1 (and_1_out, not_1_out, not_3_out);
  and and_2 (and_2_out, numero[2], numero[0]);
  and and_3 (and_3_out, not_2_out, not_3_out);
  and and_4 (and_4_out, numero[1], numero[0]);
  or or_1 (c, not_2_out, numero[0], numero[2]);
  and and_5 (and_5_out, not_1_out, not_3_out);
  and and_6 (and_6_out, not_1_out, numero[1]);
  and and_7 (and_7_out, numero[1], not_3_out);
  and and_8 (and_8_out, numero[2], not_2_out, numero[0]);
  and and_9 (and_9_out, not_1_out, not_3_out);
  and and_10 (and_10_out, numero[1], not_3_out);
  and and_11 (and_11_out, not_2_out, not_3_out);
  and and_12 (and_12_out, numero[2], not_2_out);
  and and_13 (and_13_out, numero[2], not_3_out);
  and and_14 (and_14_out, not_1_out, numero[1]);
  and and_15 (and_15_out, numero[2], not_2_out);
  and and_16 (and_16_out, numero[2], not_3_out);
  or or_2 (a, and_1_out, numero[1], and_2_out, numero[3]);
  or or_3 (b, not_1_out, and_3_out, and_4_out);
  or or_4 (d, and_5_out, and_6_out, and_7_out, and_8_out, numero[3]);
  or or_5 (e, and_9_out, and_10_out);
  or or_6 (f, and_11_out, and_12_out, and_13_out, numero[3]);
  or or_7 (g, and_14_out, and_15_out, and_16_out, numero[3]);
endmodule

module complemento_2 (
  input  [7:0] Entrada_numero,
  output [7:0] Salida_complemento
);

  wire [7:0] xor_1_out;

  xor xor_1 (xor_1_out[0], Entrada_numero[0], Entrada_numero[7]);
  xor xor_2 (xor_1_out[1], Entrada_numero[1], Entrada_numero[7]);
  xor xor_3 (xor_1_out[2], Entrada_numero[2], Entrada_numero[7]);
  xor xor_4 (xor_1_out[3], Entrada_numero[3], Entrada_numero[7]);
  xor xor_5 (xor_1_out[4], Entrada_numero[4], Entrada_numero[7]);
  xor xor_6 (xor_1_out[5], Entrada_numero[5], Entrada_numero[7]);
  xor xor_7 (xor_1_out[6], Entrada_numero[6], Entrada_numero[7]);
  xor xor_8 (xor_1_out[7], Entrada_numero[7], Entrada_numero[7]);
  Adder adder_1 (.a(xor_1_out), .b({8{1'b0}}), .out(Salida_complemento), .cin(Entrada_numero[7]));  // open: cout
endmodule

module view_number (
  input  [7:0] in_1,
  output Signo,
  output [3:0] centenas,
  output [3:0] Decenas,
  output [3:0] Unidades
);

  wire [7:0] complemento_2_1_salida_complemento, divider_1_out, divider_1_rem, divider_2_out, divider_2_rem;

  BitSelector bitselector_1 (.in(in_1), .out(Signo), .sel(3'b111));
  complemento_2 complemento_2_1 (.Entrada_numero(in_1), .Salida_complemento(complemento_2_1_salida_complemento));
  Divider divider_1 (
    .a(complemento_2_1_salida_complemento), .b(8'ha), .out(divider_1_out), .rem(divider_1_rem));  // open: upper
  Divider divider_2 (.a(divider_1_out), .b(8'ha), .out(divider_2_out), .rem(divider_2_rem));  // open: upper
  Bit_Extender #(.out_width(4)) bit_extender_1 (.in(divider_2_out), .out(centenas));
  Bit_Extender #(.out_width(4)) bit_extender_2 (.in(divider_2_rem), .out(Decenas));
  Bit_Extender #(.out_width(4)) bit_extender_3 (.in(divider_1_rem), .out(Unidades));
endmodule

module maquina_estados (
  input  Reset,
  input  Clock,
  input  [1:0] Fase,
  output Z
);

  wire and_1_out, and_2_out, and_3_out, and_4_out, and_5_out, and_6_out, and_7_out, JK0_q, JK1_q, JK2_q,
       not_1_out, or_1_out;

  not not_1 (not_1_out, Clock);
  and and_1 (and_1_out, ~Fase[0], JK1_q, JK0_q);  // AND_Gate
  and and_2 (and_2_out, ~Fase[1], JK0_q);  // AND_Gate
  or or_1 (or_1_out, ~Fase[1], ~Fase[0]);  // OR_Gate
  and and_3 (and_3_out, JK1_q, JK0_q);
  J_K_Flip_Flop JK2 (.J(and_1_out), .K(and_3_out), .clk(not_1_out), .Q(JK2_q), .reset(Reset));  // open: Qn, preset
  J_K_Flip_Flop JK1 (.J(and_2_out), .K(JK0_q), .clk(not_1_out), .Q(JK1_q), .reset(Reset));  // open: Qn, preset
  J_K_Flip_Flop JK0 (.J(or_1_out), .K(1'b1), .clk(not_1_out), .Q(JK0_q), .reset(Reset));  // open: Qn, preset
  and and_4 (and_4_out, JK2_q, JK1_q, JK0_q);
  and and_5 (and_5_out, Fase[0], JK1_q, JK0_q);
  and and_6 (and_6_out, Fase[1], JK0_q);
  and and_7 (and_7_out, Fase[1], Fase[0]);
  or or_2 (Z, and_4_out, and_5_out, and_6_out, and_7_out);

  // Other names for the same wires on the sheet: Y = Fase[0]; X = Fase[1]
endmodule

module pruba (
  input  Q3,
  input  Q2,
  input  Q1,
  input  Q0,
  output J3,
  output K3,
  output J2,
  output K2,
  output J1,
  output K1,
  output J0,
  output K0
);

  and and_1 (J3, Q2, Q1);
  and and_2 (K3, Q2, Q1);

  assign J0 = 1'b0;
  assign J1 = 1'b1;
  assign J2 = Q1;
  assign K1 = 1'b1;
  assign K2 = Q1;
endmodule

module contador_unidad (
  input  entrada_contador,
  input  clock,
  input  reset,
  output [3:0] out_4
);

  wire not_1_out, not_2_out, not_3_out;

  J_K_Flip_Flop j_k_ff_1 (
    .J(entrada_contador), .K(entrada_contador), .clk(clock), .Q(out_4[0]), .reset(reset));  // open: Qn, preset
  not not_1 (not_1_out, out_4[0]);
  J_K_Flip_Flop j_k_ff_2 (
    .J(entrada_contador), .K(entrada_contador), .clk(not_1_out), .Q(out_4[1]), .reset(reset));  // open: Qn, preset
  not not_2 (not_2_out, out_4[1]);
  J_K_Flip_Flop j_k_ff_3 (
    .J(entrada_contador), .K(entrada_contador), .clk(not_2_out), .Q(out_4[2]), .reset(reset));  // open: Qn, preset
  not not_3 (not_3_out, out_4[2]);
  J_K_Flip_Flop j_k_ff_4 (
    .J(entrada_contador), .K(entrada_contador), .clk(not_3_out), .Q(out_4[3]), .reset(reset));  // open: Qn, preset

  // Other names for the same wires on the sheet: A0 = out_4[0]; A1 = out_4[1]; A2 = out_4[2]; A3 = out_4[3]
endmodule

module contador_par (
  input  reset,
  input  clock,
  output [3:0] salida_par
);

  wire and_1_out;

  J_K_Flip_Flop jk3 (.J(and_1_out), .K(and_1_out), .clk(clock), .Q(salida_par[3]), .reset(reset));  // open: Qn, preset
  J_K_Flip_Flop jk2 (
    .J(salida_par[1]), .K(salida_par[1]), .clk(clock), .Q(salida_par[2]), .reset(reset));  // open: Qn, preset
  J_K_Flip_Flop jk1 (.J(1'b1), .K(1'b1), .clk(clock), .Q(salida_par[1]), .reset(reset));  // open: Qn, preset
  J_K_Flip_Flop jk0 (.J(1'b0), .clk(clock), .Q(salida_par[0]), .reset(reset));  // open: K, Qn, preset
  and and_1 (and_1_out, salida_par[2], salida_par[1]);

  // Other names for the same wires on the sheet: D = salida_par[0]; C = salida_par[1]; B = salida_par[2];
  //   A = salida_par[3]
endmodule
