// Logisim project sumador.circ as structural Verilog: 2 circuits, main circuit Sumador
module Sumador (
  input  A,
  input  B,
  input  Cin,
  output S,
  output Cout
);

  wire and_1_out, and_2_out, xor_1_out;

  and and_1 (and_1_out, A, B);
  or or_1 (Cout, and_1_out, and_2_out);
  xor xor_1 (xor_1_out, A, B);
  and and_2 (and_2_out, xor_1_out, Cin);
  xor xor_2 (S, xor_1_out, Cin);
endmodule

module sumador8 (
  input  [7:0] A,
  input  [7:0] B,
  input  Cin,
  output out_4,
  output [7:0] out_5
);

  wire sumador_1_cout, sumador_2_cout, sumador_3_cout, sumador_4_cout, sumador_5_cout, sumador_6_cout,
       sumador_7_cout, sumador_8_cout, xor_1_out, xor_3_out, xor_4_out, xor_5_out, xor_6_out, xor_7_out,
       xor_8_out, xor_9_out;

  xor xor_1 (xor_1_out, Cin, B[7]);
  Sumador sumador_1 (.A(A[7]), .B(xor_1_out), .Cin(sumador_2_cout), .S(out_5[7]), .Cout(sumador_1_cout));
  xor xor_2 (out_4, Cin, sumador_1_cout);
  xor xor_3 (xor_3_out, Cin, B[6]);
  Sumador sumador_2 (.A(A[6]), .B(xor_3_out), .Cin(sumador_3_cout), .S(out_5[6]), .Cout(sumador_2_cout));
  xor xor_4 (xor_4_out, Cin, B[5]);
  Sumador sumador_3 (.A(A[5]), .B(xor_4_out), .Cin(sumador_4_cout), .S(out_5[5]), .Cout(sumador_3_cout));
  xor xor_5 (xor_5_out, Cin, B[4]);
  Sumador sumador_4 (.A(A[4]), .B(xor_5_out), .Cin(sumador_5_cout), .S(out_5[4]), .Cout(sumador_4_cout));
  xor xor_6 (xor_6_out, Cin, B[3]);
  Sumador sumador_5 (.A(A[3]), .B(xor_6_out), .Cin(sumador_6_cout), .S(out_5[3]), .Cout(sumador_5_cout));
  xor xor_7 (xor_7_out, Cin, B[2]);
  Sumador sumador_6 (.A(A[2]), .B(xor_7_out), .Cin(sumador_7_cout), .S(out_5[2]), .Cout(sumador_6_cout));
  xor xor_8 (xor_8_out, Cin, B[1]);
  Sumador sumador_7 (.A(A[1]), .B(xor_8_out), .Cin(sumador_8_cout), .S(out_5[1]), .Cout(sumador_7_cout));
  xor xor_9 (xor_9_out, Cin, B[0]);
  Sumador sumador_8 (.A(A[0]), .B(xor_9_out), .Cin(Cin), .S(out_5[0]), .Cout(sumador_8_cout));
endmodule
